// Logisim project cpu.circ as structural Verilog
module adder_half (
  input  A,
  input  B,
  output SUM,
  output CARRY
);

  xor xor_1 (SUM, A, B);
  and and_1 (CARRY, A, B);
endmodule

module adder_full (
  input  A,
  input  B,
  input  C_IN,
  output SUM,
  output C_OUT
);

  wire adder_half_1_carry, adder_half_1_sum, adder_half_2_carry;

  adder_half adder_half_1 (.A(A), .B(B), .SUM(adder_half_1_sum), .CARRY(adder_half_1_carry));
  adder_half adder_half_2 (.A(adder_half_1_sum), .B(C_IN), .SUM(SUM), .CARRY(adder_half_2_carry));
  or or_1 (C_OUT, adder_half_1_carry, adder_half_2_carry);
endmodule

module adder_4bit (
  input  C_IN,
  input  [3:0] A,
  input  [3:0] B,
  output [3:0] SUM,
  output C_OUT
);

  wire adder_full_1_c_out, adder_full_2_c_out, adder_full_3_c_out;

  adder_full adder_full_1 (.SUM(SUM[0]), .C_OUT(adder_full_1_c_out), .A(C_IN), .B(A[0]), .C_IN(B[0]));
  adder_full adder_full_2 (.SUM(SUM[1]), .C_OUT(adder_full_2_c_out), .A(adder_full_1_c_out), .B(A[1]), .C_IN(B[1]));
  adder_full adder_full_3 (.SUM(SUM[2]), .C_OUT(adder_full_3_c_out), .A(adder_full_2_c_out), .B(A[2]), .C_IN(B[2]));
  adder_full adder_full_4 (.SUM(SUM[3]), .C_OUT(C_OUT), .A(adder_full_3_c_out), .B(A[3]), .C_IN(B[3]));
endmodule

module adder_8bit (
  input  C_IN,
  input  [7:0] A,
  input  [7:0] B,
  output [7:0] SUM,
  output OVERFLOW
);

  wire adder_4bit_1_c_out;

  adder_4bit adder_4bit_1 (.C_IN(C_IN), .A(A[3:0]), .B(B[3:0]), .SUM(SUM[3:0]), .C_OUT(adder_4bit_1_c_out));
  adder_4bit adder_4bit_2 (.C_IN(adder_4bit_1_c_out), .A(A[7:4]), .B(B[7:4]), .SUM(SUM[7:4]), .C_OUT(OVERFLOW));
endmodule

module ALU (
  input  [7:0] A,
  input  [7:0] B,
  input  SUBTRACT,
  output [7:0] OUT
);

  wire [7:0] bit_extender_1_out, xor_1_out;

  assign bit_extender_1_out = {{7{SUBTRACT}}, SUBTRACT};  // Bit_Extender bit_extender_1
  assign xor_1_out = B ^ bit_extender_1_out;  // XOR_Gate xor_1, 8 bits wide
  adder_8bit adder_8bit_1 (.C_IN(SUBTRACT), .A(A), .B(xor_1_out), .SUM(OUT));  // open: OVERFLOW
endmodule

module register_1bit (
  input  CLK,
  input  D,
  input  LOAD,
  input  EN,
  output Q
);

  wire and_1_out, and_2_out, not_1_out, or_1_out, Q_t;

  and and_1 (and_1_out, D, LOAD);
  not not_1 (not_1_out, LOAD);
  or or_1 (or_1_out, and_1_out, and_2_out);
  and and_2 (and_2_out, Q_t, not_1_out);
  d_flip_flop d_flip_flop_1 (.CLK(CLK), .D(or_1_out), .Q(Q_t));  // open: Q_NOT
  assign Q = EN ? Q_t : 1'bz;  // Controlled_Buffer controlled_buffer_1
endmodule

module d_flip_flop (
  input  CLK,
  input  D,
  output Q,
  output Q_NOT
);

  wire and_1_out, and_2_out, not_1_out;

  not not_1 (not_1_out, D);
  and and_1 (and_1_out, not_1_out, CLK);
  and and_2 (and_2_out, CLK, D);
  nor nor_1 (Q, and_1_out, Q_NOT);
  nor nor_2 (Q_NOT, Q, and_2_out);
endmodule

module register_8bit (
  input  [7:0] D,
  input  CLK,
  input  LOAD,
  input  EN,
  output [7:0] Q
);

  register_1bit register_1bit_1 (.CLK(CLK), .D(D[7]), .LOAD(LOAD), .EN(EN), .Q(Q[7]));
  register_1bit register_1bit_2 (.CLK(CLK), .D(D[6]), .LOAD(LOAD), .EN(EN), .Q(Q[6]));
  register_1bit register_1bit_3 (.CLK(CLK), .D(D[5]), .LOAD(LOAD), .EN(EN), .Q(Q[5]));
  register_1bit register_1bit_4 (.CLK(CLK), .D(D[4]), .LOAD(LOAD), .EN(EN), .Q(Q[4]));
  register_1bit register_1bit_5 (.CLK(CLK), .D(D[3]), .LOAD(LOAD), .EN(EN), .Q(Q[3]));
  register_1bit register_1bit_6 (.CLK(CLK), .D(D[2]), .LOAD(LOAD), .EN(EN), .Q(Q[2]));
  register_1bit register_1bit_7 (.CLK(CLK), .D(D[1]), .LOAD(LOAD), .EN(EN), .Q(Q[1]));
  register_1bit register_1bit_8 (.CLK(CLK), .D(D[0]), .LOAD(LOAD), .EN(EN), .Q(Q[0]));
endmodule

// A
module register_A (
  input  IN_0,
  input  IN_1,
  input  IN_2,
  input  IN_3,
  input  IN_4,
  input  LOAD,
  input  IN_5,
  input  IN_6,
  input  ENABLE,
  input  IN_7,
  output OUT_0,
  output OUT_1,
  output OUT_2,
  output OUT_3,
  output OUT_4,
  output OUT_5,
  output OUT_6,
  output OUT_7,
  output [7:0] DEBUG,
  output Q_0,
  output Q_1,
  output Q_2,
  output Q_3,
  output Q_4,
  output Q_5,
  output Q_6,
  output Q_7
);

  wire clock_1_out;

  Clock clock_1 (.out(clock_1_out));
  Register register_1 (
    .D({IN_7, IN_6, IN_5, IN_4, IN_3, IN_2, IN_1, IN_0}), .en(LOAD), .Q(DEBUG), .clk(clock_1_out));  // open: clr
  assign {OUT_7, OUT_6, OUT_5, OUT_4, OUT_3, OUT_2, OUT_1, OUT_0} = ENABLE ? DEBUG : 8'bz;  // Controlled_Buffer controlled_buffer_1

  assign Q_0 = DEBUG[0];
  assign Q_1 = DEBUG[1];
  assign Q_2 = DEBUG[2];
  assign Q_3 = DEBUG[3];
  assign Q_4 = DEBUG[4];
  assign Q_5 = DEBUG[5];
  assign Q_6 = DEBUG[6];
  assign Q_7 = DEBUG[7];
endmodule

module multiplexor_4bit (
  input  IN,
  input  [3:0] ADDRESS,
  output [15:0] OUT
);

  wire NA0, NA1, NA2, NA3;

  // Probe on ADDRESS
  not not_1 (NA0, ADDRESS[0]);
  not not_2 (NA1, ADDRESS[1]);
  not not_3 (NA2, ADDRESS[2]);
  not not_4 (NA3, ADDRESS[3]);
  and and_1 (OUT[0], NA0, NA1, NA2, NA3, IN);
  and and_2 (OUT[1], ADDRESS[0], NA1, NA2, NA3, IN);
  and and_3 (OUT[2], NA0, ADDRESS[1], NA2, NA3, IN);
  and and_4 (OUT[3], ADDRESS[0], ADDRESS[1], NA2, NA3, IN);
  and and_5 (OUT[4], NA0, NA1, ADDRESS[2], NA3, IN);
  and and_6 (OUT[5], ADDRESS[0], NA1, ADDRESS[2], NA3, IN);
  and and_7 (OUT[6], NA0, ADDRESS[1], ADDRESS[2], NA3, IN);
  and and_8 (OUT[7], ADDRESS[0], ADDRESS[1], ADDRESS[2], NA3, IN);
  and and_9 (OUT[8], NA0, NA1, NA2, ADDRESS[3], IN);
  and and_10 (OUT[9], ADDRESS[0], NA1, NA2, ADDRESS[3], IN);
  and and_11 (OUT[10], NA0, ADDRESS[1], NA2, ADDRESS[3], IN);
  and and_12 (OUT[11], ADDRESS[0], ADDRESS[1], NA2, ADDRESS[3], IN);
  and and_13 (OUT[12], NA0, NA1, ADDRESS[2], ADDRESS[3], IN);
  and and_14 (OUT[13], ADDRESS[0], NA1, ADDRESS[2], ADDRESS[3], IN);
  and and_15 (OUT[14], NA0, ADDRESS[1], ADDRESS[2], ADDRESS[3], IN);
  and and_16 (OUT[15], ADDRESS[0], ADDRESS[1], ADDRESS[2], ADDRESS[3], IN);

  // Other names for the same wires on the sheet: A0 = ADDRESS[0]; A1 = ADDRESS[1]; A2 = ADDRESS[2]; A3 = ADDRESS[3]
endmodule

module ram (
  input  CLK,
  input  [7:0] D,
  input  LOAD,
  input  [3:0] ADDRESS,
  input  EN,
  output [7:0] Q
);

  wire register_a_1_p6, register_a_1_p7, register_a_2_p16, register_a_2_p17, register_a_3_p16,
       register_a_3_p17, register_a_4_p16, register_a_4_p17, register_a_5_p16, register_a_5_p17,
       register_a_6_p16, register_a_6_p17, register_a_7_p16, register_a_7_p17, register_a_8_p16,
       register_a_8_p17, register_a_9_p16, register_a_9_p17, register_a_10_p16, register_a_10_p17,
       register_a_11_p16, register_a_11_p17, register_a_12_p16, register_a_12_p17, register_a_13_p16,
       register_a_13_p17, register_a_14_p16, register_a_14_p17, register_a_15_p16, register_a_15_p17;
  wire [15:0] multiplexor_4bit_1_out, multiplexor_4bit_2_out;

  multiplexor_4bit multiplexor_4bit_1 (.IN(LOAD), .ADDRESS(ADDRESS), .OUT(multiplexor_4bit_1_out));
  multiplexor_4bit multiplexor_4bit_2 (.IN(EN), .ADDRESS(ADDRESS), .OUT(multiplexor_4bit_2_out));
  // register_A register_a_1: pin names not known; wires that end beside it: D, multiplexor_4bit_1_out[0], CLK, multiplexor_4bit_2_out[0], Q, register_a_1_p6, register_a_1_p7, D
  // register_A register_a_2: pin names not known; wires that end beside it: multiplexor_4bit_1_out[0], CLK, multiplexor_4bit_2_out[0], multiplexor_4bit_2_out[0], multiplexor_4bit_2_out[0], multiplexor_4bit_2_out[0], Q, register_a_1_p6, register_a_1_p7, Q, D, multiplexor_4bit_1_out[1], CLK, multiplexor_4bit_2_out[1], Q, register_a_2_p16, register_a_2_p17, D
  // register_A register_a_3: pin names not known; wires that end beside it: multiplexor_4bit_1_out[1], CLK, multiplexor_4bit_2_out[1], multiplexor_4bit_2_out[1], multiplexor_4bit_2_out[1], multiplexor_4bit_2_out[1], Q, register_a_2_p16, register_a_2_p17, Q, D, multiplexor_4bit_1_out[2], CLK, multiplexor_4bit_2_out[2], Q, register_a_3_p16, register_a_3_p17, D
  // register_A register_a_4: pin names not known; wires that end beside it: multiplexor_4bit_1_out[2], CLK, multiplexor_4bit_2_out[2], multiplexor_4bit_2_out[2], multiplexor_4bit_2_out[2], multiplexor_4bit_2_out[2], Q, register_a_3_p16, register_a_3_p17, Q, D, multiplexor_4bit_1_out[3], CLK, multiplexor_4bit_2_out[3], Q, register_a_4_p16, register_a_4_p17, D
  // register_A register_a_5: pin names not known; wires that end beside it: multiplexor_4bit_1_out[3], CLK, multiplexor_4bit_2_out[3], multiplexor_4bit_2_out[3], multiplexor_4bit_2_out[3], multiplexor_4bit_2_out[3], Q, register_a_4_p16, register_a_4_p17, Q, D, multiplexor_4bit_1_out[4], CLK, multiplexor_4bit_2_out[4], Q, register_a_5_p16, register_a_5_p17, D
  // register_A register_a_6: pin names not known; wires that end beside it: multiplexor_4bit_1_out[4], CLK, multiplexor_4bit_2_out[4], multiplexor_4bit_2_out[4], multiplexor_4bit_2_out[4], multiplexor_4bit_2_out[4], Q, register_a_5_p16, register_a_5_p17, Q, D, multiplexor_4bit_1_out[5], CLK, multiplexor_4bit_2_out[5], Q, register_a_6_p16, register_a_6_p17, D
  // register_A register_a_7: pin names not known; wires that end beside it: multiplexor_4bit_1_out[5], CLK, multiplexor_4bit_2_out[5], multiplexor_4bit_2_out[5], multiplexor_4bit_2_out[5], multiplexor_4bit_2_out[5], Q, register_a_6_p16, register_a_6_p17, Q, D, multiplexor_4bit_1_out[6], CLK, multiplexor_4bit_2_out[6], Q, register_a_7_p16, register_a_7_p17, D
  // register_A register_a_8: pin names not known; wires that end beside it: multiplexor_4bit_1_out[6], CLK, multiplexor_4bit_2_out[6], multiplexor_4bit_2_out[6], multiplexor_4bit_2_out[6], multiplexor_4bit_2_out[6], Q, register_a_7_p16, register_a_7_p17, Q, D, multiplexor_4bit_1_out[7], CLK, multiplexor_4bit_2_out[7], Q, register_a_8_p16, register_a_8_p17, D
  // register_A register_a_9: pin names not known; wires that end beside it: multiplexor_4bit_1_out[7], CLK, multiplexor_4bit_2_out[7], multiplexor_4bit_2_out[7], multiplexor_4bit_2_out[7], multiplexor_4bit_2_out[7], Q, register_a_8_p16, register_a_8_p17, Q, D, multiplexor_4bit_1_out[8], CLK, multiplexor_4bit_2_out[8], Q, register_a_9_p16, register_a_9_p17, D
  // register_A register_a_10: pin names not known; wires that end beside it: multiplexor_4bit_1_out[8], CLK, multiplexor_4bit_2_out[8], multiplexor_4bit_2_out[8], multiplexor_4bit_2_out[8], multiplexor_4bit_2_out[8], Q, register_a_9_p16, register_a_9_p17, Q, D, multiplexor_4bit_1_out[9], CLK, multiplexor_4bit_2_out[9], Q, register_a_10_p16, register_a_10_p17, D
  // register_A register_a_11: pin names not known; wires that end beside it: multiplexor_4bit_1_out[9], CLK, multiplexor_4bit_2_out[9], multiplexor_4bit_2_out[9], multiplexor_4bit_2_out[9], multiplexor_4bit_2_out[9], Q, register_a_10_p16, register_a_10_p17, Q, D, multiplexor_4bit_1_out[10], CLK, multiplexor_4bit_2_out[10], Q, register_a_11_p16, register_a_11_p17, D
  // register_A register_a_12: pin names not known; wires that end beside it: multiplexor_4bit_1_out[10], CLK, multiplexor_4bit_2_out[10], multiplexor_4bit_2_out[10], multiplexor_4bit_2_out[10], multiplexor_4bit_2_out[10], Q, register_a_11_p16, register_a_11_p17, Q, D, multiplexor_4bit_1_out[11], CLK, multiplexor_4bit_2_out[11], Q, register_a_12_p16, register_a_12_p17, D
  // register_A register_a_13: pin names not known; wires that end beside it: multiplexor_4bit_1_out[11], CLK, multiplexor_4bit_2_out[11], multiplexor_4bit_2_out[11], multiplexor_4bit_2_out[11], multiplexor_4bit_2_out[11], Q, register_a_12_p16, register_a_12_p17, Q, D, multiplexor_4bit_1_out[12], CLK, multiplexor_4bit_2_out[12], Q, register_a_13_p16, register_a_13_p17, D
  // register_A register_a_14: pin names not known; wires that end beside it: multiplexor_4bit_1_out[12], CLK, multiplexor_4bit_2_out[12], multiplexor_4bit_2_out[12], multiplexor_4bit_2_out[12], multiplexor_4bit_2_out[12], Q, register_a_13_p16, register_a_13_p17, Q, D, multiplexor_4bit_1_out[13], CLK, multiplexor_4bit_2_out[13], Q, register_a_14_p16, register_a_14_p17, D
  // register_A register_a_15: pin names not known; wires that end beside it: multiplexor_4bit_1_out[13], CLK, multiplexor_4bit_2_out[13], multiplexor_4bit_2_out[13], multiplexor_4bit_2_out[13], multiplexor_4bit_2_out[13], Q, register_a_14_p16, register_a_14_p17, Q, D, multiplexor_4bit_1_out[14], CLK, multiplexor_4bit_2_out[14], Q, register_a_15_p16, register_a_15_p17, D
  // register_A register_a_16: pin names not known; wires that end beside it: multiplexor_4bit_1_out[14], CLK, multiplexor_4bit_2_out[14], multiplexor_4bit_2_out[14], multiplexor_4bit_2_out[14], multiplexor_4bit_2_out[14], Q, register_a_15_p16, register_a_15_p17, Q, D, multiplexor_4bit_1_out[15], CLK, multiplexor_4bit_2_out[15], Q
endmodule

// CNT
module counter_4bit (
  input  ENABLE,
  input  [3:0] IN,
  output [3:0] OUT
);

  wire clock_1_out, j_k_ff_1_qn, j_k_ff_2_qn, j_k_ff_3_qn;
  wire [3:0] not_1_out;

  Clock clock_1 (.out(clock_1_out));
  assign not_1_out = ~IN;  // NOT_Gate not_1, 4 bits wide
  J_K_Flip_Flop j_k_ff_1 (
    .J(1'b1), .clk(clock_1_out), .K(1'b1), .Q(OUT[0]), .Qn(j_k_ff_1_qn), .preset(IN[3]), .en(ENABLE),
    .reset(not_1_out[3]));
  J_K_Flip_Flop j_k_ff_2 (
    .J(1'b1), .clk(j_k_ff_1_qn), .K(1'b1), .Q(OUT[1]), .Qn(j_k_ff_2_qn), .preset(IN[2]), .en(ENABLE),
    .reset(not_1_out[2]));
  J_K_Flip_Flop j_k_ff_3 (
    .J(1'b1), .clk(j_k_ff_2_qn), .K(1'b1), .Q(OUT[2]), .Qn(j_k_ff_3_qn), .preset(IN[1]), .en(ENABLE),
    .reset(not_1_out[1]));
  J_K_Flip_Flop j_k_ff_4 (
    .J(1'b1), .clk(j_k_ff_3_qn), .K(1'b1), .Q(OUT[3]), .preset(IN[0]), .en(ENABLE), .reset(not_1_out[0]));  // open: Qn
endmodule

module CPU (
  input  CI,
  input  J,
  input  CE,
  input  AI,
  input  AO,
  input  BI,
  input  BO,
  input  OI,
  input  [7:0] in_9,
  input  in_10
);

  wire pc_1_out_1, pc_1_out_2, pc_1_out_3;
  wire [3:0] pc_1_debug;
  wire [7:0] b_1_debug, controlled_buffer_1_out, out_1_debug;

  // Probe on controlled_buffer_1_out
  assign controlled_buffer_1_out = in_10 ? in_9 : 8'bz;  // Controlled_Buffer controlled_buffer_1
  Pull_Resistor pull_resistor_1 (.node(controlled_buffer_1_out));
  // Probe on pc_1_debug
  PC pc_1 (
    .IN_0(controlled_buffer_1_out[0]), .IN_1(pc_1_out_1), .IN_2(pc_1_out_2), .IN_3(pc_1_out_3),
    .OUT_0(controlled_buffer_1_out[0]), .OUT_1(pc_1_out_1), .OUT_2(pc_1_out_2), .OUT_3(pc_1_out_3), .J(J),
    .CE(CE), .CO(CI), .DEBUG(pc_1_debug));
  register_A register_a_1 (
    .LOAD(AI), .ENABLE(AO), .IN_0(controlled_buffer_1_out[0]), .IN_1(controlled_buffer_1_out[1]),
    .IN_2(controlled_buffer_1_out[2]), .IN_3(controlled_buffer_1_out[3]), .IN_4(controlled_buffer_1_out[4]),
    .IN_5(controlled_buffer_1_out[5]), .IN_6(controlled_buffer_1_out[6]), .IN_7(controlled_buffer_1_out[7]),
    .OUT_0(controlled_buffer_1_out[0]), .OUT_1(controlled_buffer_1_out[1]),
    .OUT_2(controlled_buffer_1_out[2]), .OUT_3(controlled_buffer_1_out[3]),
    .OUT_4(controlled_buffer_1_out[4]), .OUT_5(controlled_buffer_1_out[5]),
    .OUT_6(controlled_buffer_1_out[6]), .OUT_7(controlled_buffer_1_out[7]));  // open: DEBUG, Q_0, Q_1, Q_2, Q_3, Q_4, Q_5, Q_6, Q_7
  // Probe on nothing
  // Probe on b_1_debug
  B b_1 (
    .IN_0(controlled_buffer_1_out[0]), .IN_1(controlled_buffer_1_out[1]), .IN_2(controlled_buffer_1_out[2]),
    .IN_3(controlled_buffer_1_out[3]), .IN_4(controlled_buffer_1_out[4]), .LOAD(BI),
    .IN_5(controlled_buffer_1_out[5]), .IN_6(controlled_buffer_1_out[6]), .IN_7(controlled_buffer_1_out[7]),
    .OUT_0(controlled_buffer_1_out[0]), .OUT_1(controlled_buffer_1_out[1]),
    .OUT_2(controlled_buffer_1_out[2]), .OUT_3(controlled_buffer_1_out[3]),
    .OUT_4(controlled_buffer_1_out[4]), .OUT_5(controlled_buffer_1_out[5]),
    .OUT_6(controlled_buffer_1_out[6]), .OUT_7(controlled_buffer_1_out[7]), .DEBUG(b_1_debug), .ENABLE(BO));  // open: Q_0, Q_1, Q_2, Q_3, Q_4, Q_5, Q_6, Q_7
  OUT out_1 (.LOAD(OI), .DEBUG(out_1_debug));  // open: IN_0, IN_1, IN_2, IN_3, IN_4, IN_5, IN_6, IN_7
  // Probe on out_1_debug
endmodule

module PC (
  input  IN_0,
  input  IN_1,
  input  IN_2,
  input  J,
  input  IN_3,
  input  CE,
  input  CO,
  output [3:0] DEBUG,
  output OUT_0,
  output OUT_1,
  output OUT_2,
  output OUT_3
);

  wire [3:0] controlled_buffer_1_out;

  assign controlled_buffer_1_out = J ? {IN_3, IN_2, IN_1, IN_0} : 4'bz;  // Controlled_Buffer controlled_buffer_1
  assign {OUT_3, OUT_2, OUT_1, OUT_0} = CO ? DEBUG : 4'bz;  // Controlled_Buffer controlled_buffer_2
  counter_4bit counter_4bit_1 (.ENABLE(CE), .IN(controlled_buffer_1_out), .OUT(DEBUG));
endmodule

module B (
  input  IN_0,
  input  IN_1,
  input  IN_2,
  input  IN_3,
  input  IN_4,
  input  LOAD,
  input  IN_5,
  input  IN_6,
  input  ENABLE,
  input  IN_7,
  output OUT_0,
  output OUT_1,
  output OUT_2,
  output OUT_3,
  output OUT_4,
  output OUT_5,
  output OUT_6,
  output OUT_7,
  output [7:0] DEBUG,
  output Q_0,
  output Q_1,
  output Q_2,
  output Q_3,
  output Q_4,
  output Q_5,
  output Q_6,
  output Q_7
);

  wire clock_1_out;

  Clock clock_1 (.out(clock_1_out));
  Register register_1 (
    .D({IN_7, IN_6, IN_5, IN_4, IN_3, IN_2, IN_1, IN_0}), .en(LOAD), .Q(DEBUG), .clk(clock_1_out));  // open: clr
  assign {OUT_7, OUT_6, OUT_5, OUT_4, OUT_3, OUT_2, OUT_1, OUT_0} = ENABLE ? DEBUG : 8'bz;  // Controlled_Buffer controlled_buffer_1

  assign Q_0 = DEBUG[0];
  assign Q_1 = DEBUG[1];
  assign Q_2 = DEBUG[2];
  assign Q_3 = DEBUG[3];
  assign Q_4 = DEBUG[4];
  assign Q_5 = DEBUG[5];
  assign Q_6 = DEBUG[6];
  assign Q_7 = DEBUG[7];
endmodule

module OUT (
  input  IN_0,
  input  IN_1,
  input  IN_2,
  input  IN_3,
  input  IN_4,
  input  LOAD,
  input  IN_5,
  input  IN_6,
  input  IN_7,
  output [7:0] DEBUG
);

  wire clock_1_out;

  Clock clock_1 (.out(clock_1_out));
  Register register_1 (
    .D({IN_7, IN_6, IN_5, IN_4, IN_3, IN_2, IN_1, IN_0}), .en(LOAD), .Q(DEBUG), .clk(clock_1_out));  // open: clr
  DotMatrix #(.inputtype("row"), .matrixcols(12)) dotmatrix_1 ();  // open: row0, row1, row2, row3, row4, row5, row6
endmodule

module decoder (
  output _100_A,
  output _10_A,
  output _1_A,
  output _100_B,
  output _10_B,
  output _1_B,
  output _10_C,
  output _10_C_2,
  output _1_C,
  output _10_D,
  output _10_D_2,
  output _1_D,
  output _10_E,
  output _10_E_2,
  output _1_E,
  output _10_F,
  output _10_F_2,
  output _1_F,
  output _10_G,
  output _10_G_2,
  output _1_G,
  output _10_DOT,
  output _10_DOT_2,
  output _1_DOT
);
endmodule
